# Fritzing sketch wiring (saved by Fritzing 0.9.3b)
breadboards: 1

parts:
  U3 = NodeMCU V1.0
  LED1 = RGB LED (com. cathode, rgb) [package="5 mm [THT]"]
  R2 = Resistor [tolerance=±5% resistance=220 package=THT]
  R3 = Resistor [tolerance=±5% resistance=220 package=THT]
  R4 = Resistor [tolerance=±5% resistance=220 package=THT]

nets:
  N1: U3.D0, R3.Pin_1
  N2: U3.D1, R2.Pin_1
  N3: U3.D2, R4.Pin_1
  N4: LED1.red_anode, R3.Pin_0
  N5: LED1.green_anode, R2.Pin_0
  N6: LED1.blue_anode, R4.Pin_0

custom parts:
  NodeMCU V1.0: ESP8266 based NodeMCU
